// Logisim project riscv_cpu_schematic.circ as structural Verilog: 19 circuits, main circuit Data Path
module Top (
);

  wire mem_control_1_iload_sel, mem_control_1_memload_sel;
  wire [3:0] data_path_1_wea, mem_control_1_dwea, mem_control_1_iwea;
  wire [11:0] data_path_1_dmem_adr_2;
  wire [31:0] bios_memory_1_doutb, bios_memory_1_doutb_2, data_memory_1_douta, data_path_1_dmem_adr,
       data_path_1_dmem_wdata, instruction_memory_1_doutb, multiplexer_1_out, multiplexer_2_out, PC;

  Instruction_Memory instruction_memory_1 (
    .addrb(PC[15:2]), .addra({data_path_1_dmem_adr[15:14], data_path_1_dmem_adr_2}),
    .dina(data_path_1_dmem_wdata), .wea(mem_control_1_dwea), .doutb(instruction_memory_1_doutb));  // open: clk
  BIOS_Memory bios_memory_1 (
    .addrb(data_path_1_dmem_adr_2), .addra(PC[13:2]), .doutb(bios_memory_1_doutb),
    .doutb_2(bios_memory_1_doutb_2));  // open: clk
  Multiplexer #(.width(32)) multiplexer_1 (
    .in0(instruction_memory_1_doutb), .in1(bios_memory_1_doutb_2), .out(multiplexer_1_out),
    .sel(mem_control_1_iload_sel));  // open: en
  Data_Path data_path_1 (
    .PC(PC), .idoutb(multiplexer_1_out),
    .dmem_adr({data_path_1_dmem_adr[31:14], data_path_1_dmem_adr_2, data_path_1_dmem_adr[1:0]}),
    .dmem_wdata(data_path_1_dmem_wdata), .wea(data_path_1_wea), .din(multiplexer_2_out));
  Mem_Control mem_control_1 (
    .wea(data_path_1_wea), .iwea(mem_control_1_iwea), .dwea(mem_control_1_dwea), .PC_Upper_bits(PC[31:28]),
    .Data_adr_Upper_bits(data_path_1_dmem_adr[31:28]), .memload_sel(mem_control_1_memload_sel),
    .iload_sel(mem_control_1_iload_sel));  // open: IOstore_en, mem_or_IO
  Data_Memory data_memory_1 (
    .addra({data_path_1_dmem_adr[15:14], data_path_1_dmem_adr_2}), .dina(data_path_1_dmem_wdata),
    .wea(mem_control_1_iwea), .douta(data_memory_1_douta));  // open: clk
  Multiplexer #(.width(32)) multiplexer_2 (
    .in0(data_memory_1_douta), .in1(bios_memory_1_doutb), .out(multiplexer_2_out),
    .sel(mem_control_1_memload_sel));  // open: en
endmodule

module Data_Path (
  input  [31:0] din,
  input  [31:0] idoutb,
  output [3:0] wea,
  output [31:0] dmem_adr,
  output [31:0] dmem_wdata,
  output [31:0] PC
);

  wire branchD, control_path_1_inst_or_rs2, control_path_1_jop, control_path_1_regwrite,
       hazard_unit_1_flushe, hazard_unit_1_stalld, hazard_unit_1_stallf, not_1_out, not_2_out, register_14_q,
       register_15_q, register_23_q, register_29_q;
  wire [1:0] control_path_1_opasel, control_path_1_pcsel_bit0, control_path_1_wbsel, Forward1D, Forward2D,
       hazard_unit_1_forward1e, hazard_unit_1_forward2e, register_11_q, register_13_q, register_22_q,
       register_28_q;
  wire [2:0] pre_decoder_1_funct3, register_7_q, register_20_q;
  wire [4:0] control_path_1_aluctl, pre_decoder_1_addr1, pre_decoder_1_addr2, pre_decoder_1_rd,
       pre_decoder_1_shamt, register_3_q, register_5_q, register_10_q, register_16_q, register_17_q,
       register_18_q, register_24_q;
  wire [6:0] pre_decoder_1_funct7, pre_decoder_1_opcode;
  wire [31:0] adder_1_out, alu_1_alu_out, branchtargen_1_btarg, data_alignment_1_out_4, jtargen_1_jtarg,
       jtargen_1_jtargplus4, multiplexer_2_out, multiplexer_3_out, multiplexer_4_out, multiplexer_5_out,
       multiplexer_6_out, multiplexer_7_out, multiplexer_8_out, pre_decoder_1_immextend, Program_Counter_q,
       register_1_q, register_2_q, register_4_q, register_6_q, register_8_q, register_9_q, register_12_q,
       register_19_q, register_21_q, register_25_q, register_26_q, register_27_q,
       register_file_1_rs1_data_out, register_file_1_rs2_address_out;

  Multiplexer #(.select(2), .width(32)) multiplexer_1 (
    .in0(adder_1_out), .in1(jtargen_1_jtarg), .in2(branchtargen_1_btarg), .out(PC),
    .sel(control_path_1_pcsel_bit0));  // open: in3, en
  not not_1 (not_1_out, hazard_unit_1_stallf);
  Register #(.width(32)) Program_Counter (.D(PC), .en(not_1_out), .Q(Program_Counter_q));  // open: clk, clr
  Adder #(.width(32)) adder_1 (.a(Program_Counter_q), .b(32'h4), .out(adder_1_out));  // open: cin, cout
  not not_2 (not_2_out, hazard_unit_1_stalld);
  Register #(.width(32)) register_1 (
    .D(idoutb), .en(not_2_out), .Q(register_1_q), .clr(control_path_1_pcsel_bit0[1]));  // open: clk
  Register #(.width(32)) register_2 (
    .D(Program_Counter_q), .en(not_2_out), .Q(register_2_q), .clr(control_path_1_pcsel_bit0[1]));  // open: clk
  Pre_Decoder pre_decoder_1 (
    .instr(register_1_q), .ImmExtend(pre_decoder_1_immextend), .rd(pre_decoder_1_rd),
    .funct3(pre_decoder_1_funct3), .addr1(pre_decoder_1_addr1), .addr2(pre_decoder_1_addr2),
    .shamt(pre_decoder_1_shamt), .funct7(pre_decoder_1_funct7), .Opcode(pre_decoder_1_opcode));
  Register_File register_file_1 (
    .Data_In(multiplexer_8_out), .wd(register_29_q), .rs1_data_out(register_file_1_rs1_data_out),
    .rs1_address(pre_decoder_1_addr1), .Data_Address(register_24_q),
    .rs2_address_out(register_file_1_rs2_address_out), .rs2_address(pre_decoder_1_addr2));  // open: clk
  Control_Path control_path_1 (
    .Opcode(pre_decoder_1_opcode), .funct3(pre_decoder_1_funct3), .inst_bit30(pre_decoder_1_funct7[5]),
    .RegWrite(control_path_1_regwrite), .Inst_or_rs2(control_path_1_inst_or_rs2),
    .OpASel(control_path_1_opasel), .WBSel(control_path_1_wbsel), .PCSel_bit0(control_path_1_pcsel_bit0[0]),
    .ALUCtl(control_path_1_aluctl), .branch(branchD), .JOp(control_path_1_jop));  // open: ExtendSel, shamt
  Multiplexer #(.select(2), .width(32)) multiplexer_2 (
    .in0(register_file_1_rs1_data_out), .in1(multiplexer_8_out), .in2(register_19_q),
    .out(multiplexer_2_out), .sel(Forward1D));  // open: in3, en
  JTarGen jtargen_1 (
    .PC(register_2_q), .Jimm(pre_decoder_1_immextend), .rs1(multiplexer_2_out), .Jop(control_path_1_jop),
    .JTarg(jtargen_1_jtarg), .JTargPlus4(jtargen_1_jtargplus4));
  BranchTarGen branchtargen_1 (
    .BImm(pre_decoder_1_immextend), .PC(register_2_q), .BTarg(branchtargen_1_btarg), .rs1(multiplexer_2_out),
    .rs2(multiplexer_3_out), .PCSel_bit1(control_path_1_pcsel_bit0[1]), .branch(branchD),
    .funct3(pre_decoder_1_funct3));
  Multiplexer #(.select(2), .width(32)) multiplexer_3 (
    .in0(register_file_1_rs2_address_out), .in1(multiplexer_8_out), .in2(register_19_q),
    .out(multiplexer_3_out), .sel(Forward2D));  // open: in3, en
  Register #(.width(5)) register_3 (
    .D(pre_decoder_1_rd), .Q(register_3_q), .clr(hazard_unit_1_flushe));  // open: en, clk
  Register #(.width(32)) register_4 (
    .D(multiplexer_2_out), .Q(register_4_q), .clr(hazard_unit_1_flushe));  // open: en, clk
  Register #(.width(5)) register_5 (
    .D(pre_decoder_1_shamt), .Q(register_5_q), .clr(hazard_unit_1_flushe));  // open: en, clk
  Register #(.width(32)) register_6 (
    .D(multiplexer_3_out), .Q(register_6_q), .clr(hazard_unit_1_flushe));  // open: en, clk
  Register #(.width(3)) register_7 (
    .D(pre_decoder_1_funct3), .Q(register_7_q), .clr(hazard_unit_1_flushe));  // open: en, clk
  Register #(.width(32)) register_8 (
    .D(pre_decoder_1_immextend), .Q(register_8_q), .clr(hazard_unit_1_flushe));  // open: en, clk
  Register #(.width(32)) register_9 (
    .D(jtargen_1_jtargplus4), .Q(register_9_q), .clr(hazard_unit_1_flushe));  // open: en, clk
  Register #(.width(5)) register_10 (
    .D(control_path_1_aluctl), .Q(register_10_q), .clr(hazard_unit_1_flushe));  // open: en, clk
  Register #(.width(2)) register_11 (
    .D(control_path_1_opasel), .Q(register_11_q), .clr(hazard_unit_1_flushe));  // open: en, clk
  Register #(.width(32)) register_12 (
    .D(register_2_q), .Q(register_12_q), .clr(hazard_unit_1_flushe));  // open: en, clk
  Register #(.width(2)) register_13 (
    .D(control_path_1_wbsel), .Q(register_13_q), .clr(hazard_unit_1_flushe));  // open: en, clk
  Register #(.width(1)) register_14 (
    .D(control_path_1_regwrite), .Q(register_14_q), .clr(hazard_unit_1_flushe));  // open: en, clk
  Register #(.width(1)) register_15 (
    .D(control_path_1_inst_or_rs2), .Q(register_15_q), .clr(hazard_unit_1_flushe));  // open: en, clk
  Register #(.width(5)) register_16 (
    .D(pre_decoder_1_addr1), .Q(register_16_q), .clr(hazard_unit_1_flushe));  // open: en, clk
  Register #(.width(5)) register_17 (
    .D(pre_decoder_1_addr2), .Q(register_17_q), .clr(hazard_unit_1_flushe));  // open: en, clk
  Multiplexer #(.select(2), .width(32)) multiplexer_4 (
    .in0(register_4_q), .in1(multiplexer_8_out), .in2(register_19_q), .out(multiplexer_4_out),
    .sel(hazard_unit_1_forward1e));  // open: in3, en
  Multiplexer #(.select(2), .width(32)) multiplexer_5 (
    .in0(register_6_q), .in1(multiplexer_8_out), .in2(register_19_q), .out(multiplexer_5_out),
    .sel(hazard_unit_1_forward2e));  // open: in3, en
  Multiplexer #(.select(2), .width(32)) multiplexer_6 (
    .in0(multiplexer_4_out), .in1(register_12_q), .in2({32{1'b0}}), .out(multiplexer_6_out),
    .sel(register_11_q));  // open: in3, en
  Multiplexer #(.width(32)) multiplexer_7 (
    .in0(multiplexer_5_out), .in1(register_8_q), .out(multiplexer_7_out), .sel(register_15_q));  // open: en
  ALU alu_1 (
    .A(multiplexer_6_out), .B(multiplexer_7_out), .ALU_Control(register_10_q), .ALU_Out(alu_1_alu_out),
    .shamt(register_5_q));  // open: Zero
  Register #(.width(5)) register_18 (.D(register_3_q), .Q(register_18_q));  // open: en, clk, clr
  Register #(.width(32)) register_19 (.D(alu_1_alu_out), .Q(register_19_q));  // open: en, clk, clr
  Register #(.width(3)) register_20 (.D(register_7_q), .Q(register_20_q));  // open: en, clk, clr
  Register #(.width(32)) register_21 (.D(register_9_q), .Q(register_21_q));  // open: en, clk, clr
  Register #(.width(2)) register_22 (.D(register_13_q), .Q(register_22_q));  // open: en, clk, clr
  Register #(.width(1)) register_23 (.D(register_14_q), .Q(register_23_q));  // open: en, clk, clr
  Hazard_Unit hazard_unit_1 (
    .adr1E(register_16_q), .rdM(register_18_q), .rdW(register_24_q), .RegWriteM(register_23_q),
    .RegWriteW(register_29_q), .adr2E(register_17_q), .Forward1E(hazard_unit_1_forward1e),
    .Forward2E(hazard_unit_1_forward2e), .adr1D(pre_decoder_1_addr1), .adr2D(pre_decoder_1_addr2),
    .rdE(register_3_q), .WBSelE(register_13_q), .StallF(hazard_unit_1_stallf), .StallD(hazard_unit_1_stalld),
    .FlushE(hazard_unit_1_flushe), .Forward1D(Forward1D), .Forward2D(Forward2D), .branchD(branchD),
    .RegWriteE(register_14_q), .JumpD(control_path_1_pcsel_bit0[0]));
  Store_Mask_Gen store_mask_gen_1 (.funct3(register_20_q), .sft(register_19_q[1:0]), .SMask(wea));
  Data_Alignment data_alignment_1 (
    .Data(din), .out_4(data_alignment_1_out_4), .funct3(register_20_q), .Shift(register_19_q[1:0]));
  Register #(.width(5)) register_24 (.D(register_18_q), .Q(register_24_q));  // open: en, clk, clr
  Register #(.width(32)) register_25 (.D(data_alignment_1_out_4), .Q(register_25_q));  // open: en, clk, clr
  Register #(.width(32)) register_26 (.D(register_19_q), .Q(register_26_q));  // open: en, clk, clr
  Register #(.width(32)) register_27 (.D(register_21_q), .Q(register_27_q));  // open: en, clk, clr
  Register #(.width(2)) register_28 (.D(register_22_q), .Q(register_28_q));  // open: en, clk, clr
  Register #(.width(1)) register_29 (.D(register_23_q), .Q(register_29_q));  // open: en, clk, clr
  Multiplexer #(.select(2), .width(32)) multiplexer_8 (
    .in0(register_26_q), .in1(register_25_q), .in2(register_27_q), .out(multiplexer_8_out),
    .sel(register_28_q));  // open: in3, en

  // Notes on the sheet:
  //   PC Plus 4
  //   Register File
  //   ALU
  //   result
endmodule

module Hazard_Unit (
  input  [4:0] adr1E,
  input  [4:0] rdM,
  input  [4:0] rdW,
  input  RegWriteM,
  input  RegWriteW,
  input  [4:0] adr2E,
  input  [4:0] adr1D,
  input  [4:0] adr2D,
  input  [4:0] rdE,
  input  [1:0] WBSelE,
  input  RegWriteE,
  input  branchD,
  input  JumpD,
  output [1:0] Forward1E,
  output [1:0] Forward2E,
  output StallF,
  output StallD,
  output FlushE,
  output [1:0] Forward1D,
  output [1:0] Forward2D
);

  wire and_2_out, and_4_out, and_5_out, and_6_out, and_8_out, and_10_out, comparator_1_eq, comparator_2_eq,
       comparator_3_eq, comparator_4_eq, comparator_5_eq, comparator_6_eq, comparator_7_eq, comparator_8_eq,
       comparator_9_eq, comparator_10_eq, comparator_11_eq, comparator_12_eq, comparator_13_eq,
       comparator_14_eq, not_1_out, not_2_out, not_3_out, not_4_out, not_5_out, not_6_out, not_7_out,
       not_8_out, not_9_out, or_1_out;

  Comparator #(.width(5), .mode("unsigned")) comparator_1 (.a(adr1D), .b(rdE), .eq(comparator_1_eq));  // open: gt, lt
  Comparator #(.width(5), .mode("unsigned")) comparator_2 (.a(adr2D), .b(rdE), .eq(comparator_2_eq));  // open: gt, lt
  Comparator #(.width(5), .mode("unsigned")) comparator_3 (
    .a(adr1E), .b({5{1'b0}}), .eq(comparator_3_eq));  // open: gt, lt
  Comparator #(.width(5), .mode("unsigned")) comparator_4 (.a(adr1E), .b(rdM), .eq(comparator_4_eq));  // open: gt, lt
  Comparator #(.width(5), .mode("unsigned")) comparator_5 (.a(adr1E), .b(rdW), .eq(comparator_5_eq));  // open: gt, lt
  Comparator #(.width(5), .mode("unsigned")) comparator_6 (
    .a(adr2E), .b({5{1'b0}}), .eq(comparator_6_eq));  // open: gt, lt
  Comparator #(.width(5), .mode("unsigned")) comparator_7 (.a(adr2E), .b(rdM), .eq(comparator_7_eq));  // open: gt, lt
  Comparator #(.width(5), .mode("unsigned")) comparator_8 (.a(adr2E), .b(rdW), .eq(comparator_8_eq));  // open: gt, lt
  or or_1 (or_1_out, comparator_1_eq, comparator_2_eq);
  Comparator #(.width(5), .mode("unsigned")) comparator_9 (
    .a(adr1D), .b({5{1'b0}}), .eq(comparator_9_eq));  // open: gt, lt
  Comparator #(.width(5), .mode("unsigned")) comparator_10 (.a(adr1D), .b(rdM), .eq(comparator_10_eq));  // open: gt, lt
  Comparator #(.width(5), .mode("unsigned")) comparator_11 (.a(adr1D), .b(rdW), .eq(comparator_11_eq));  // open: gt, lt
  Comparator #(.width(5), .mode("unsigned")) comparator_12 (
    .a(adr2D), .b({5{1'b0}}), .eq(comparator_12_eq));  // open: gt, lt
  Comparator #(.width(5), .mode("unsigned")) comparator_13 (.a(adr2D), .b(rdM), .eq(comparator_13_eq));  // open: gt, lt
  Comparator #(.width(5), .mode("unsigned")) comparator_14 (.a(adr2D), .b(rdW), .eq(comparator_14_eq));  // open: gt, lt
  not not_1 (not_1_out, comparator_3_eq);
  not not_2 (not_2_out, comparator_6_eq);
  not not_3 (not_3_out, WBSelE[1]);
  not not_4 (not_4_out, comparator_9_eq);
  not not_5 (not_5_out, comparator_12_eq);
  and and_1 (Forward1E[1], not_1_out, comparator_4_eq, RegWriteM);
  and and_2 (and_2_out, not_1_out, comparator_5_eq, RegWriteW);
  and and_3 (Forward2E[1], not_2_out, comparator_7_eq, RegWriteM);
  and and_4 (and_4_out, not_2_out, comparator_8_eq, RegWriteW);
  and and_5 (and_5_out, or_1_out, WBSelE[0], not_3_out);
  and and_6 (and_6_out, or_1_out, RegWriteE, branchD);
  and and_7 (Forward1D[1], not_4_out, RegWriteM, comparator_10_eq);
  and and_8 (and_8_out, not_4_out, comparator_11_eq, RegWriteW);
  and and_9 (Forward2D[1], not_5_out, RegWriteM, comparator_13_eq);
  and and_10 (and_10_out, not_5_out, comparator_14_eq, RegWriteW);
  not not_6 (not_6_out, Forward1E[1]);
  not not_7 (not_7_out, Forward2E[1]);
  not not_8 (not_8_out, Forward1D[1]);
  not not_9 (not_9_out, Forward2D[1]);
  and and_11 (Forward1E[0], not_6_out, and_2_out);
  and and_12 (Forward2E[0], not_7_out, and_4_out);
  or or_2 (FlushE, and_5_out, JumpD, and_6_out);
  and and_13 (Forward1D[0], not_8_out, and_8_out);
  and and_14 (Forward2D[0], not_9_out, and_10_out);

  assign StallD = FlushE;
  assign StallF = FlushE;
endmodule

module Register_File (
  input  [31:0] Data_In,
  input  wd,
  input  [4:0] rs1_address,
  input  [4:0] Data_Address,
  input  [4:0] rs2_address,
  input  clk,
  output [31:0] rs1_data_out,
  output [31:0] rs2_address_out
);

  wire and_1_out, and_2_out, and_3_out, and_4_out, and_5_out, and_6_out, and_7_out, and_8_out, and_9_out,
       and_10_out, and_11_out, and_12_out, and_13_out, and_14_out, and_15_out, and_16_out, and_17_out,
       and_18_out, and_19_out, and_20_out, and_21_out, and_22_out, and_23_out, and_24_out, and_25_out,
       and_26_out, and_27_out, and_28_out, and_29_out, and_30_out, and_31_out, decoder_1_out1,
       decoder_1_out2, decoder_1_out3, decoder_1_out4, decoder_1_out5, decoder_1_out6, decoder_1_out7,
       decoder_1_out8, decoder_1_out9, decoder_1_out10, decoder_1_out11, decoder_1_out12, decoder_1_out13,
       decoder_1_out14, decoder_1_out15, decoder_1_out16, decoder_1_out17, decoder_1_out18, decoder_1_out19,
       decoder_1_out20, decoder_1_out21, decoder_1_out22, decoder_1_out23, decoder_1_out24, decoder_1_out25,
       decoder_1_out26, decoder_1_out27, decoder_1_out28, decoder_1_out29, decoder_1_out30, decoder_1_out31;
  wire [31:0] register_1_q, register_2_q, register_3_q, register_4_q, register_5_q, register_6_q,
       register_7_q, register_8_q, register_9_q, register_10_q, register_11_q, register_12_q, register_13_q,
       register_14_q, register_15_q, register_16_q, register_17_q, register_18_q, register_19_q,
       register_20_q, register_21_q, register_22_q, register_23_q, register_24_q, register_25_q,
       register_26_q, register_27_q, register_28_q, register_29_q, register_30_q, register_31_q,
       register_32_q;

  Decoder #(.select(5)) decoder_1 (
    .out1(decoder_1_out1), .out2(decoder_1_out2), .out3(decoder_1_out3), .out4(decoder_1_out4),
    .out5(decoder_1_out5), .out6(decoder_1_out6), .out7(decoder_1_out7), .out8(decoder_1_out8),
    .out9(decoder_1_out9), .out10(decoder_1_out10), .out11(decoder_1_out11), .out12(decoder_1_out12),
    .out13(decoder_1_out13), .out14(decoder_1_out14), .out15(decoder_1_out15), .out16(decoder_1_out16),
    .out17(decoder_1_out17), .out18(decoder_1_out18), .out19(decoder_1_out19), .out20(decoder_1_out20),
    .out21(decoder_1_out21), .out22(decoder_1_out22), .out23(decoder_1_out23), .out24(decoder_1_out24),
    .out25(decoder_1_out25), .out26(decoder_1_out26), .out27(decoder_1_out27), .out28(decoder_1_out28),
    .out29(decoder_1_out29), .out30(decoder_1_out30), .out31(decoder_1_out31), .sel(Data_Address));  // open: out0, en
  Register #(.width(32)) register_1 (.D({32{1'b0}}), .en(1'b0), .Q(register_1_q), .clk(clk), .clr(1'b0));
  Register #(.width(32)) register_2 (.D(Data_In), .en(and_1_out), .Q(register_2_q), .clk(clk), .clr(1'b0));
  and and_1 (and_1_out, decoder_1_out4, wd);
  Register #(.width(32)) register_3 (.D(Data_In), .en(and_2_out), .Q(register_3_q), .clk(clk), .clr(1'b0));
  and and_2 (and_2_out, decoder_1_out8, wd);
  Register #(.width(32)) register_4 (.D(Data_In), .en(and_3_out), .Q(register_4_q), .clk(clk), .clr(1'b0));
  and and_3 (and_3_out, decoder_1_out12, wd);
  Register #(.width(32)) register_5 (.D(Data_In), .en(and_4_out), .Q(register_5_q), .clk(clk), .clr(1'b0));
  and and_4 (and_4_out, decoder_1_out16, wd);
  Register #(.width(32)) register_6 (.D(Data_In), .en(and_5_out), .Q(register_6_q), .clk(clk), .clr(1'b0));
  and and_5 (and_5_out, decoder_1_out20, wd);
  Register #(.width(32)) register_7 (.D(Data_In), .en(and_6_out), .Q(register_7_q), .clk(clk), .clr(1'b0));
  and and_6 (and_6_out, decoder_1_out24, wd);
  Register #(.width(32)) register_8 (.D(Data_In), .en(and_7_out), .Q(register_8_q), .clk(clk), .clr(1'b0));
  and and_7 (and_7_out, decoder_1_out28, wd);
  and and_8 (and_8_out, decoder_1_out1, wd);
  and and_9 (and_9_out, decoder_1_out5, wd);
  and and_10 (and_10_out, decoder_1_out9, wd);
  and and_11 (and_11_out, decoder_1_out13, wd);
  and and_12 (and_12_out, decoder_1_out17, wd);
  and and_13 (and_13_out, decoder_1_out21, wd);
  and and_14 (and_14_out, decoder_1_out25, wd);
  and and_15 (and_15_out, decoder_1_out29, wd);
  Register #(.width(32)) register_9 (.D(Data_In), .en(and_8_out), .Q(register_9_q), .clk(clk), .clr(1'b0));
  Register #(.width(32)) register_10 (.D(Data_In), .en(and_9_out), .Q(register_10_q), .clk(clk), .clr(1'b0));
  Register #(.width(32)) register_11 (.D(Data_In), .en(and_10_out), .Q(register_11_q), .clk(clk), .clr(1'b0));
  Register #(.width(32)) register_12 (.D(Data_In), .en(and_11_out), .Q(register_12_q), .clk(clk), .clr(1'b0));
  Register #(.width(32)) register_13 (.D(Data_In), .en(and_12_out), .Q(register_13_q), .clk(clk), .clr(1'b0));
  Register #(.width(32)) register_14 (.D(Data_In), .en(and_13_out), .Q(register_14_q), .clk(clk), .clr(1'b0));
  Register #(.width(32)) register_15 (.D(Data_In), .en(and_14_out), .Q(register_15_q), .clk(clk), .clr(1'b0));
  Register #(.width(32)) register_16 (.D(Data_In), .en(and_15_out), .Q(register_16_q), .clk(clk), .clr(1'b0));
  Register #(.width(32)) register_17 (.D(Data_In), .en(and_16_out), .Q(register_17_q), .clk(clk), .clr(1'b0));
  and and_16 (and_16_out, decoder_1_out2, wd);
  Register #(.width(32)) register_18 (.D(Data_In), .en(and_17_out), .Q(register_18_q), .clk(clk), .clr(1'b0));
  and and_17 (and_17_out, decoder_1_out6, wd);
  Register #(.width(32)) register_19 (.D(Data_In), .en(and_18_out), .Q(register_19_q), .clk(clk), .clr(1'b0));
  and and_18 (and_18_out, decoder_1_out10, wd);
  Register #(.width(32)) register_20 (.D(Data_In), .en(and_19_out), .Q(register_20_q), .clk(clk), .clr(1'b0));
  and and_19 (and_19_out, decoder_1_out14, wd);
  Register #(.width(32)) register_21 (.D(Data_In), .en(and_20_out), .Q(register_21_q), .clk(clk), .clr(1'b0));
  and and_20 (and_20_out, decoder_1_out18, wd);
  Register #(.width(32)) register_22 (.D(Data_In), .en(and_21_out), .Q(register_22_q), .clk(clk), .clr(1'b0));
  and and_21 (and_21_out, decoder_1_out22, wd);
  Register #(.width(32)) register_23 (.D(Data_In), .en(and_22_out), .Q(register_23_q), .clk(clk), .clr(1'b0));
  and and_22 (and_22_out, decoder_1_out26, wd);
  Register #(.width(32)) register_24 (.D(Data_In), .en(and_23_out), .Q(register_24_q), .clk(clk), .clr(1'b0));
  and and_23 (and_23_out, decoder_1_out30, wd);
  and and_24 (and_24_out, decoder_1_out3, wd);
  and and_25 (and_25_out, decoder_1_out7, wd);
  and and_26 (and_26_out, decoder_1_out11, wd);
  and and_27 (and_27_out, decoder_1_out15, wd);
  and and_28 (and_28_out, decoder_1_out19, wd);
  and and_29 (and_29_out, decoder_1_out23, wd);
  and and_30 (and_30_out, decoder_1_out27, wd);
  and and_31 (and_31_out, decoder_1_out31, wd);
  Register #(.width(32)) register_25 (.D(Data_In), .en(and_24_out), .Q(register_25_q), .clk(clk), .clr(1'b0));
  Register #(.width(32)) register_26 (.D(Data_In), .en(and_25_out), .Q(register_26_q), .clk(clk), .clr(1'b0));
  Register #(.width(32)) register_27 (.D(Data_In), .en(and_26_out), .Q(register_27_q), .clk(clk), .clr(1'b0));
  Register #(.width(32)) register_28 (.D(Data_In), .en(and_27_out), .Q(register_28_q), .clk(clk), .clr(1'b0));
  Register #(.width(32)) register_29 (.D(Data_In), .en(and_28_out), .Q(register_29_q), .clk(clk), .clr(1'b0));
  Register #(.width(32)) register_30 (.D(Data_In), .en(and_29_out), .Q(register_30_q), .clk(clk), .clr(1'b0));
  Register #(.width(32)) register_31 (.en(and_30_out), .Q(register_31_q), .clk(clk), .clr(1'b0));  // open: D
  Register #(.width(32)) register_32 (.D(Data_In), .en(and_31_out), .Q(register_32_q), .clk(clk), .clr(1'b0));
  Multiplexer #(.select(5), .width(32)) multiplexer_1 (
    .in0(register_1_q), .in1(register_9_q), .in2(register_17_q), .in3(register_25_q), .in4(register_2_q),
    .in5(register_10_q), .in6(register_18_q), .in7(register_26_q), .in8(register_3_q), .in9(register_11_q),
    .in10(register_19_q), .in11(register_27_q), .in12(register_4_q), .in13(register_12_q),
    .in14(register_20_q), .in15(register_28_q), .in16(register_5_q), .in17(register_13_q),
    .in18(register_21_q), .in19(register_29_q), .in20(register_6_q), .in21(register_14_q),
    .in22(register_22_q), .in23(register_30_q), .in24(register_7_q), .in25(register_15_q),
    .in26(register_23_q), .in27(register_31_q), .in28(register_8_q), .in29(register_16_q),
    .in30(register_24_q), .in31(register_32_q), .out(rs1_data_out), .sel(rs1_address));  // open: en
  Multiplexer #(.select(5), .width(32)) multiplexer_2 (
    .in0(register_1_q), .in1(register_9_q), .in2(register_17_q), .in3(register_25_q), .in4(register_2_q),
    .in5(register_10_q), .in6(register_18_q), .in7(register_26_q), .in8(register_3_q), .in9(register_11_q),
    .in10(register_19_q), .in11(register_27_q), .in12(register_4_q), .in13(register_12_q),
    .in14(register_20_q), .in15(register_28_q), .in16(register_5_q), .in17(register_13_q),
    .in18(register_21_q), .in19(register_29_q), .in20(register_6_q), .in21(register_14_q),
    .in22(register_22_q), .in23(register_30_q), .in24(register_7_q), .in25(register_15_q),
    .in26(register_23_q), .in27(register_31_q), .in28(register_8_q), .in29(register_16_q),
    .in30(register_24_q), .in31(register_32_q), .out(rs2_address_out), .sel(rs2_address));  // open: en

  // Notes on the sheet:
  //   rs1
endmodule

module Data_Alignment (
  input  [31:0] Data,
  input  [2:0] funct3,
  input  [1:0] Shift,
  output [31:0] out_4
);

  wire [4:0] bit_extender_1_out, multiplier_1_out;
  wire [31:0] bit_extender_2_out, bit_extender_3_out, bit_extender_4_out, bit_extender_5_out, shifter_1_out;

  assign bit_extender_1_out = {{3{1'b0}}, Shift};  // Bit_Extender bit_extender_1
  Multiplier #(.width(5)) multiplier_1 (
    .a(5'b01000), .b(bit_extender_1_out), .out(multiplier_1_out));  // open: cin, cout
  Shifter #(.width(32), .shift("lr")) shifter_1 (.in(Data), .\dist (multiplier_1_out), .out(shifter_1_out));
  assign bit_extender_2_out = {{24{shifter_1_out[7]}}, shifter_1_out[7:0]};  // Bit_Extender bit_extender_2
  assign bit_extender_3_out = {{24{1'b0}}, shifter_1_out[7:0]};  // Bit_Extender bit_extender_3
  assign bit_extender_4_out = {{16{shifter_1_out[15]}}, shifter_1_out[15:0]};  // Bit_Extender bit_extender_4
  assign bit_extender_5_out = {{16{1'b0}}, shifter_1_out[15:0]};  // Bit_Extender bit_extender_5
  Multiplexer #(.select(3), .width(32)) multiplexer_1 (
    .in0(bit_extender_2_out), .in1(bit_extender_4_out), .in2(Data), .in4(bit_extender_3_out),
    .in5(bit_extender_5_out), .out(out_4), .sel(funct3));  // open: in3, in6, in7, en
endmodule

module ALU (
  input  [31:0] A,
  input  [31:0] B,
  input  [4:0] shamt,
  input  [4:0] ALU_Control,
  output [31:0] ALU_Out,
  output Zero
);

  wire comparator_1_lt, comparator_2_eq, multiplexer_2_out;
  wire [2:1] undriven;
  wire [31:0] adder_1_out, and_1_out, bit_extender_1_out, multiplexer_1_out, multiplexer_3_out, not_1_out,
       or_1_out, shifter_1_out, shifter_2_out, shifter_3_out, shifter_4_out, xor_1_out;

  assign not_1_out = ~B;  // NOT_Gate not_1, 32 bits wide
  Shifter #(.width(32)) shifter_1 (.in(B), .\dist (shamt), .out(shifter_1_out));
  Multiplexer #(.select(2), .width(32)) multiplexer_1 (
    .in0(B), .in1(shifter_1_out), .in3(not_1_out), .out(multiplexer_1_out), .sel(ALU_Control[4:3]));  // open: in2, en
  Comparator #(.width(32), .mode("unsigned")) comparator_1 (
    .a(A), .b(multiplexer_1_out), .lt(comparator_1_lt));  // open: gt, eq
  Adder #(.width(32)) adder_1 (.a(A), .b(multiplexer_1_out), .out(adder_1_out), .cin(ALU_Control[4]));  // open: cout
  assign and_1_out = A & multiplexer_1_out;  // AND_Gate and_1, 32 bits wide
  assign or_1_out = A | multiplexer_1_out;  // OR_Gate or_1, 32 bits wide
  assign xor_1_out = A ^ multiplexer_1_out;  // XOR_Gate xor_1, 32 bits wide
  Shifter #(.width(32)) shifter_2 (.in(A), .\dist (multiplexer_1_out[24:20]), .out(shifter_2_out));
  Shifter #(.width(32), .shift("lr")) shifter_3 (.in(A), .\dist (multiplexer_1_out[24:20]), .out(shifter_3_out));
  Shifter #(.width(32), .shift("ar")) shifter_4 (.in(A), .\dist (multiplexer_1_out[24:20]), .out(shifter_4_out));
  Multiplexer multiplexer_2 (
    .in0(comparator_1_lt), .in1(adder_1_out[31]), .out(multiplexer_2_out), .sel(ALU_Control[3]));  // open: en
  assign bit_extender_1_out = {{31{1'b0}}, multiplexer_2_out};  // Bit_Extender bit_extender_1
  Multiplexer #(.width(32)) multiplexer_3 (
    .in0(shifter_3_out), .in1(shifter_4_out), .out(multiplexer_3_out), .sel(B[10]));  // open: en
  Multiplexer #(.select(3), .width(32)) multiplexer_4 (
    .in0(adder_1_out), .in1(bit_extender_1_out), .in2(and_1_out), .in3(or_1_out), .in4(xor_1_out),
    .in5(shifter_2_out), .in6(multiplexer_3_out), .out(ALU_Out), .sel({undriven, ALU_Control[0]}));  // open: in7, en
  Comparator #(.width(32), .mode("unsigned")) comparator_2 (
    .a(ALU_Out), .b({32{1'b0}}), .eq(comparator_2_eq));  // open: gt, lt
  Multiplexer multiplexer_5 (
    .in0(comparator_2_eq), .in1(multiplexer_2_out), .out(Zero), .sel(ALU_Control[0]));  // open: en
  // Pins of 1 and 3 bits meet at {undriven, ALU_Control[0]}
endmodule

module Alignment_Check (
  input  [13:0] in_1,
  output [13:0] out_2,
  output [1:0] Address_Shift
);

  wire [13:0] divider_1_out;
  wire [13:2] divider_1_rem;

  Divider #(.width(14)) divider_1 (
    .a(in_1), .b(14'h4), .out(divider_1_out), .rem({divider_1_rem, Address_Shift}));  // open: upper
  Shifter #(.width(14)) shifter_1 (.in(divider_1_out), .\dist (4'b0010), .out(out_2));

  // Notes on the sheet:
  //   Address In
  //   Address Start
endmodule

module Instruction_Memory (
  input  [13:0] addrb,
  input  [13:0] addra,
  input  clk,
  input  [31:0] dina,
  input  [3:0] wea,
  output [31:0] doutb
);

  wire or_1_out;
  wire [7:0] transistor_1_out, transistor_2_out, transistor_3_out, transistor_4_out;
  wire [13:0] multiplexer_1_out;

  Multiplexer #(.width(14)) multiplexer_1 (
    .in0(addrb), .in1(addra), .out(multiplexer_1_out), .sel(or_1_out));  // open: en
  Transistor #(.\type ("n"), .gate("br"), .width(8)) transistor_1 (
    .in(dina[7:0]), .out(transistor_1_out), .gate(wea[0]));
  Transistor #(.\type ("n"), .gate("br"), .width(8)) transistor_2 (
    .in(dina[15:8]), .out(transistor_2_out), .gate(wea[1]));
  Transistor #(.\type ("n"), .gate("br"), .width(8)) transistor_3 (
    .in(dina[23:16]), .out(transistor_3_out), .gate(wea[2]));
  Transistor #(.\type ("n"), .gate("br"), .width(8)) transistor_4 (
    .in(dina[31:24]), .out(transistor_4_out), .gate(wea[2]));
  or or_1 (or_1_out, wea[0], wea[1], wea[2], wea[3]);
  RAM #(.addrWidth(14), .dataWidth(32), .bus("separate")) ram_1 (
    .addr(multiplexer_1_out), .din({transistor_4_out, transistor_3_out, transistor_2_out, transistor_1_out}),
    .data(doutb), .str(or_1_out), .clk(clk));  // open: sel, ld, clr
endmodule

module Data_Memory (
  input  [13:0] addra,
  input  clk,
  input  [31:0] dina,
  input  [3:0] wea,
  output [31:0] douta
);

  wire or_1_out;
  wire [7:0] transistor_1_out, transistor_2_out, transistor_3_out, transistor_4_out;

  Transistor #(.\type ("n"), .gate("br"), .width(8)) transistor_1 (
    .in(dina[7:0]), .out(transistor_1_out), .gate(wea[0]));
  Transistor #(.\type ("n"), .gate("br"), .width(8)) transistor_2 (
    .in(dina[15:8]), .out(transistor_2_out), .gate(wea[1]));
  Transistor #(.\type ("n"), .gate("br"), .width(8)) transistor_3 (
    .in(dina[23:16]), .out(transistor_3_out), .gate(wea[2]));
  Transistor #(.\type ("n"), .gate("br"), .width(8)) transistor_4 (
    .in(dina[31:24]), .out(transistor_4_out), .gate(wea[2]));
  or or_1 (or_1_out, wea[0], wea[1], wea[2], wea[3]);
  RAM #(.addrWidth(14), .dataWidth(32), .bus("separate")) ram_1 (
    .addr(addra), .din({transistor_4_out, transistor_3_out, transistor_2_out, transistor_1_out}),
    .data(douta), .str(or_1_out), .clk(clk));  // open: sel, ld, clr
endmodule

module BIOS_Memory (
  input  [11:0] addrb,
  input  [11:0] addra,
  input  clk,
  output [31:0] doutb,
  output [31:0] doutb_2
);

  RAM #(.addrWidth(12), .dataWidth(32)) ram_1 (.addr(addrb), .data(doutb), .clk(clk));  // open: sel, ld, clr
  RAM #(.addrWidth(12), .dataWidth(32)) ram_2 (.addr(addra), .data(doutb_2), .clk(clk));  // open: sel, ld, clr
endmodule

module Mem_Control (
  input  [3:0] wea,
  input  [3:0] PC_Upper_bits,
  input  [3:0] Data_adr_Upper_bits,
  output [3:0] iwea,
  output [3:0] dwea,
  output memload_sel,
  output iload_sel,
  output IOstore_en,
  output mem_or_IO
);

  wire and_2_out, and_6_out, dstore_en, istore_en, nand_1_out, not_1_out, not_2_out, not_3_out, not_4_out,
       not_5_out, not_6_out, not_7_out, not_8_out, not_9_out;

  nand nand_1 (nand_1_out, not_4_out, not_3_out, not_2_out, PC_Upper_bits[0]);
  not not_1 (not_1_out, PC_Upper_bits[0]);
  not not_2 (not_2_out, PC_Upper_bits[1]);
  not not_3 (not_3_out, PC_Upper_bits[2]);
  not not_4 (not_4_out, PC_Upper_bits[3]);
  and and_1 (iload_sel, nand_1_out, and_2_out);
  and and_2 (and_2_out, not_4_out, PC_Upper_bits[2], not_2_out, not_1_out);
  Multiplexer #(.width(4)) multiplexer_1 (.in0(4'b0000), .in1(wea), .out(iwea), .sel(istore_en));  // open: en
  Multiplexer #(.width(4)) multiplexer_2 (.in0(4'b0000), .in1(wea), .out(dwea), .sel(dstore_en));  // open: en
  not not_5 (not_5_out, Data_adr_Upper_bits[0]);
  not not_6 (not_6_out, Data_adr_Upper_bits[1]);
  not not_7 (not_7_out, Data_adr_Upper_bits[2]);
  not not_8 (not_8_out, Data_adr_Upper_bits[3]);
  and and_3 (istore_en, not_8_out, not_7_out, Data_adr_Upper_bits[2], PC_Upper_bits[2]);
  and and_4 (dstore_en, not_8_out, not_7_out, Data_adr_Upper_bits[0]);
  and and_5 (memload_sel, not_9_out, and_6_out);
  not not_9 (not_9_out, dstore_en);
  and and_6 (and_6_out, not_8_out, Data_adr_Upper_bits[2], not_6_out, not_5_out);
  and and_7 (IOstore_en, Data_adr_Upper_bits[3], not_7_out, not_6_out, not_5_out);

  assign mem_or_IO = IOstore_en;
endmodule

module BranchTarGen (
  input  [31:0] BImm,
  input  [31:0] PC,
  input  [31:0] rs1,
  input  branch,
  input  [31:0] rs2,
  input  [2:0] funct3,
  output [31:0] BTarg,
  output PCSel_bit1
);

  wire comparator_1_eq, comparator_1_lt, comparator_2_lt, multiplexer_1_out, multiplexer_2_out, not_1_out,
       not_2_out;
  wire [1:0] and_2_out;

  Adder #(.width(32)) adder_1 (.a(BImm), .b(PC), .out(BTarg));  // open: cin, cout
  Comparator #(.width(32)) comparator_1 (.a(rs1), .b(rs2), .eq(comparator_1_eq), .lt(comparator_1_lt));  // open: gt
  Comparator #(.width(32), .mode("unsigned")) comparator_2 (.a(rs1), .b(rs2), .lt(comparator_2_lt));  // open: gt, eq
  Multiplexer #(.select(2)) multiplexer_1 (
    .in0(comparator_1_eq), .in1(comparator_1_lt), .in2(comparator_2_lt), .out(multiplexer_1_out),
    .sel(and_2_out));  // open: in3, en
  and and_1 (and_2_out[1], funct3[1], funct3[2]);
  and and_2 (and_2_out[0], funct3[2], not_1_out);
  not not_1 (not_1_out, funct3[1]);
  not not_2 (not_2_out, multiplexer_1_out);
  Multiplexer multiplexer_2 (
    .in0(multiplexer_1_out), .in1(not_2_out), .out(multiplexer_2_out), .sel(funct3[0]));  // open: en
  and and_3 (PCSel_bit1, multiplexer_2_out, branch);
endmodule

module JTarGen (
  input  [31:0] Jimm,
  input  [31:0] PC,
  input  [31:0] rs1,
  input  Jop,
  output [31:0] JTarg,
  output [31:0] JTargPlus4
);

  wire [31:0] multiplexer_1_out;

  Multiplexer #(.width(32)) multiplexer_1 (.in0(PC), .in1(rs1), .out(multiplexer_1_out), .sel(Jop));  // open: en
  Adder #(.width(32)) adder_1 (.a(Jimm), .b(multiplexer_1_out), .out(JTarg));  // open: cin, cout
  Adder #(.width(32)) adder_2 (.a(JTarg), .b(32'h4), .out(JTargPlus4));  // open: cin, cout
endmodule

module Control_Path (
  input  [6:0] Opcode,
  input  [2:0] funct3,
  input  inst_bit30,
  output RegWrite,
  output Inst_or_rs2,
  output [1:0] ExtendSel,
  output [1:0] OpASel,
  output [4:0] shamt,
  output [1:0] WBSel,
  output PCSel_bit0,
  output JOp,
  output branch,
  output [4:0] ALUCtl
);

  wire inst_classifier_1_auipc, inst_classifier_1_default, inst_classifier_1_jal, inst_classifier_1_load_mem,
       inst_classifier_1_lui, inst_classifier_1_reg_imm, inst_classifier_1_reg_reg,
       inst_classifier_1_store_mem, main_decoder_1_aluop;

  Inst_Classifier inst_classifier_1 (
    .Opcode(Opcode), .load_mem(inst_classifier_1_load_mem), .store_mem(inst_classifier_1_store_mem),
    .\default (inst_classifier_1_default), .reg_imm(inst_classifier_1_reg_imm),
    .reg_reg(inst_classifier_1_reg_reg), .branch(branch), .jal(inst_classifier_1_jal), .jalr(JOp),
    .lui(inst_classifier_1_lui), .auipc(inst_classifier_1_auipc));
  Main_Decoder main_decoder_1 (
    .load_mem(inst_classifier_1_load_mem), .store_mem(inst_classifier_1_store_mem),
    .reg_imm(inst_classifier_1_reg_imm), .reg_reg(inst_classifier_1_reg_reg), .branch(branch),
    .jal(inst_classifier_1_jal), .jalr(JOp), .lui(inst_classifier_1_lui), .auipc(inst_classifier_1_auipc),
    .\default (inst_classifier_1_default), .RegWrite(RegWrite), .Inst_or_rs2(Inst_or_rs2),
    .ExtendSel(ExtendSel), .shamt(shamt), .WBSel(WBSel), .PCSel_bit0(PCSel_bit0),
    .ALUOp(main_decoder_1_aluop), .OpASel(ExtendSel));
  Mini_Decoder mini_decoder_1 (
    .load_mem(inst_classifier_1_load_mem), .store_mem(inst_classifier_1_store_mem), .funct3(funct3),
    .reg_imm(inst_classifier_1_reg_imm), .ALUOp(main_decoder_1_aluop), .reg_reg(inst_classifier_1_reg_reg),
    .branch(branch), .ALUCtl(ALUCtl), .Inst_bit30(inst_bit30));
endmodule

module Inst_Classifier (
  input  [6:0] Opcode,
  output load_mem,
  output store_mem,
  output \default ,
  output reg_imm,
  output reg_reg,
  output branch,
  output jal,
  output jalr,
  output lui,
  output auipc
);

  wire [6:0] buffer_1_out, not_1_out;

  nor nor_1 (\default , load_mem, store_mem, reg_imm, reg_reg, branch, jal, lui);
  assign buffer_1_out = Opcode;  // Buffer buffer_1, 7 bits wide
  assign not_1_out = ~Opcode;  // NOT_Gate not_1, 7 bits wide
  and and_1 (load_mem, not_1_out[6], not_1_out[5], not_1_out[4], not_1_out[3], not_1_out[2], buffer_1_out[1], buffer_1_out[0]);
  and and_2 (store_mem, not_1_out[6], buffer_1_out[5], not_1_out[4], not_1_out[3], not_1_out[2], buffer_1_out[1], buffer_1_out[0]);
  and and_3 (reg_imm, not_1_out[6], not_1_out[5], buffer_1_out[4], not_1_out[3], not_1_out[2], buffer_1_out[1], buffer_1_out[0]);
  and and_4 (reg_reg, not_1_out[6], buffer_1_out[5], buffer_1_out[4], not_1_out[3], not_1_out[2], buffer_1_out[1], buffer_1_out[0]);
  and and_5 (branch, buffer_1_out[6], buffer_1_out[5], not_1_out[4], not_1_out[3], not_1_out[2], buffer_1_out[1], buffer_1_out[0]);
  and and_6 (jal, buffer_1_out[6], buffer_1_out[5], not_1_out[4], buffer_1_out[4], buffer_1_out[2], buffer_1_out[1], buffer_1_out[0]);
  and and_7 (jalr, buffer_1_out[6], buffer_1_out[5], not_1_out[4], not_1_out[3], buffer_1_out[2], buffer_1_out[1], buffer_1_out[0]);
  and and_8 (lui, not_1_out[6], buffer_1_out[5], buffer_1_out[4], not_1_out[3], buffer_1_out[2], buffer_1_out[1], buffer_1_out[0]);
  and and_9 (auipc, not_1_out[6], not_1_out[5], buffer_1_out[4], not_1_out[3], buffer_1_out[2], buffer_1_out[1], buffer_1_out[0]);
endmodule

module Main_Decoder (
  input  load_mem,
  input  store_mem,
  input  reg_imm,
  input  reg_reg,
  input  branch,
  input  jal,
  input  jalr,
  input  lui,
  input  auipc,
  input  \default ,
  output RegWrite,
  output Inst_or_rs2,
  output [1:0] ExtendSel,
  output [1:0] OpASel,
  output [4:0] shamt,
  output [1:0] WBSel,
  output PCSel_bit0,
  output ALUOp
);

  nor nor_1 (RegWrite, branch, store_mem, \default );
  or or_1 (Inst_or_rs2, branch, reg_reg);
  or or_2 (ExtendSel[1], lui, auipc, jal);
  or or_3 (ExtendSel[0], jal, store_mem);
  or or_4 (OpASel[0], jal, auipc);
  or or_5 (shamt[3], lui, auipc);
  or or_6 (shamt[1], load_mem, store_mem);
  or or_7 (WBSel[1], jal, jalr);
  or or_8 (PCSel_bit0, jal, jalr);
  or or_9 (ALUOp, branch, reg_imm, reg_reg);

  assign OpASel[1] = lui;
  assign {shamt[4], shamt[2], shamt[0]} = {1'b0, shamt[3], 1'b0};
  assign WBSel[0] = load_mem;
endmodule

module Mini_Decoder (
  input  load_mem,
  input  store_mem,
  input  Inst_bit30,
  input  [2:0] funct3,
  input  reg_imm,
  input  ALUOp,
  input  reg_reg,
  input  branch,
  output [4:0] ALUCtl
);

  wire and_1_out, and_2_out, and_3_out, and_4_out, and_5_out, and_8_out, and_9_out, decoder_1_out0,
       decoder_1_out1, decoder_1_out2, decoder_1_out3, decoder_1_out4, decoder_1_out5, decoder_1_out6,
       decoder_1_out7, or_2_out, or_3_out, or_4_out, or_6_out, or_7_out, or_8_out, or_10_out;

  Decoder #(.select(3)) decoder_1 (
    .out0(decoder_1_out0), .out1(decoder_1_out1), .out2(decoder_1_out2), .out3(decoder_1_out3),
    .out4(decoder_1_out4), .out5(decoder_1_out5), .out6(decoder_1_out6), .out7(decoder_1_out7), .sel(funct3),
    .en(ALUOp));
  or or_1 (ALUCtl[4], branch, and_1_out, and_2_out);
  and and_1 (and_1_out, decoder_1_out0, Inst_bit30, reg_reg);
  and and_2 (and_2_out, or_2_out, or_3_out);
  or or_2 (or_2_out, decoder_1_out2, decoder_1_out3);
  or or_3 (or_3_out, reg_imm, reg_reg);
  or or_4 (or_4_out, decoder_1_out0, decoder_1_out1, decoder_1_out4, decoder_1_out5);
  or or_5 (ALUCtl[3], and_4_out, load_mem, store_mem, and_3_out, and_1_out, and_5_out);
  and and_3 (and_3_out, reg_imm, decoder_1_out2);
  and and_4 (and_4_out, or_4_out, branch);
  and and_5 (and_5_out, reg_reg, decoder_1_out2);
  and and_6 (ALUCtl[2], or_6_out, or_3_out);
  or or_6 (or_6_out, decoder_1_out4, decoder_1_out1, decoder_1_out5);
  and and_7 (ALUCtl[1], or_7_out, or_3_out);
  or or_7 (or_7_out, decoder_1_out6, decoder_1_out7, decoder_1_out5);
  and and_8 (and_8_out, or_8_out, branch);
  or or_8 (or_8_out, decoder_1_out4, decoder_1_out5, decoder_1_out6, decoder_1_out7);
  or or_9 (ALUCtl[0], and_8_out, and_9_out);
  and and_9 (and_9_out, or_10_out, or_3_out);
  or or_10 (or_10_out, decoder_1_out2, decoder_1_out3, decoder_1_out5, decoder_1_out1);
endmodule

module Store_Mask_Gen (
  input  [2:0] funct3,
  input  [1:0] sft,
  output [3:0] SMask
);

  wire [3:0] multiplexer_1_out;

  Multiplexer #(.select(2), .width(4)) multiplexer_1 (
    .in0(4'b0001), .in1(4'b0011), .in2(4'b1111), .out(multiplexer_1_out), .sel(funct3[1:0]));  // open: in3, en
  Shifter #(.width(4)) shifter_1 (.in(multiplexer_1_out), .\dist (sft), .out(SMask));
endmodule

module Pre_Decoder (
  input  [31:0] instr,
  output [6:0] Opcode,
  output [4:0] rd,
  output [2:0] funct3,
  output [4:0] addr1,
  output [4:0] addr2,
  output [4:0] shamt,
  output [6:0] funct7,
  output [31:0] ImmExtend
);

  wire and_1_out, and_2_out, inst_classifier_1_auipc, inst_classifier_1_branch, inst_classifier_1_default,
       inst_classifier_1_jal, inst_classifier_1_jalr, inst_classifier_1_load_mem, inst_classifier_1_lui,
       inst_classifier_1_reg_imm, inst_classifier_1_reg_reg, inst_classifier_1_store_mem, nand_1_out,
       nand_2_out, nand_3_out, not_1_out, or_1_out;
  wire [2:0] or_2_out;
  wire [31:0] bit_extender_1_out, bit_extender_2_out, bit_extender_3_out, bit_extender_4_out;

  Inst_Classifier inst_classifier_1 (
    .Opcode(instr[6:0]), .load_mem(inst_classifier_1_load_mem), .store_mem(inst_classifier_1_store_mem),
    .\default (inst_classifier_1_default), .reg_imm(inst_classifier_1_reg_imm),
    .reg_reg(inst_classifier_1_reg_reg), .branch(inst_classifier_1_branch), .jal(inst_classifier_1_jal),
    .jalr(inst_classifier_1_jalr), .lui(inst_classifier_1_lui), .auipc(inst_classifier_1_auipc));
  nand nand_1 (nand_1_out, inst_classifier_1_store_mem, inst_classifier_1_branch);
  Multiplexer #(.width(5)) multiplexer_1 (.in0({5{1'b0}}), .in1(instr[11:7]), .out(rd), .sel(nand_1_out));  // open: en
  assign bit_extender_1_out = {{19{instr[31]}}, {instr[31], instr[7], instr[30:25], instr[11:8], 1'b0}};  // Bit_Extender bit_extender_1
  assign bit_extender_2_out = {{20{instr[31]}}, instr[31:20]};  // Bit_Extender bit_extender_2
  assign bit_extender_3_out = {{20{1'b0}}, {instr[31:25], instr[11:7]}};  // Bit_Extender bit_extender_3
  assign bit_extender_4_out = {{11{instr[31]}}, {instr[31], instr[19:12], instr[20], instr[30:21], 1'b0}};  // Bit_Extender bit_extender_4
  nand nand_2 (nand_2_out, inst_classifier_1_lui, inst_classifier_1_auipc, inst_classifier_1_jal);
  Multiplexer #(.width(3)) multiplexer_2 (
    .in0(3'b000), .in1(instr[14:12]), .out(funct3), .sel(nand_2_out));  // open: en
  Multiplexer #(.width(5)) multiplexer_3 (
    .in0({5{1'b0}}), .in1(instr[19:15]), .out(addr1), .sel(nand_2_out));  // open: en
  nand nand_3 (nand_3_out, inst_classifier_1_lui, inst_classifier_1_auipc, inst_classifier_1_jal, inst_classifier_1_jalr, inst_classifier_1_load_mem, inst_classifier_1_reg_imm);
  Multiplexer #(.width(5)) multiplexer_4 (
    .in0({5{1'b0}}), .in1(instr[24:20]), .out(addr2), .sel(nand_3_out));  // open: en
  not not_1 (not_1_out, funct3[1]);
  and and_1 (and_1_out, funct3[0], not_1_out);
  and and_2 (and_2_out, inst_classifier_1_reg_imm, and_1_out);
  Multiplexer #(.width(5)) multiplexer_5 (
    .in0({5{1'b0}}), .in1(instr[24:20]), .out(shamt), .sel(and_2_out));  // open: en
  Multiplexer #(.select(3), .width(32)) multiplexer_6 (
    .in0(bit_extender_1_out), .in1(bit_extender_2_out), .in2(bit_extender_3_out),
    .in3({instr[31:12], {12{1'b0}}}), .in4(bit_extender_4_out), .in5({32{1'b0}}), .out(ImmExtend),
    .sel(or_2_out));  // open: in6, in7, en
  or or_1 (or_1_out, inst_classifier_1_reg_reg, and_2_out);
  Multiplexer #(.width(7)) multiplexer_7 (
    .in0({7{1'b0}}), .in1(instr[31:25]), .out(funct7), .sel(or_1_out));  // open: en
  or or_2 (or_2_out[0], inst_classifier_1_jal, inst_classifier_1_branch, inst_classifier_1_reg_reg);
  or or_3 (or_2_out[1], inst_classifier_1_jalr, inst_classifier_1_branch, inst_classifier_1_load_mem, inst_classifier_1_reg_imm);
  or or_4 (or_2_out[2], inst_classifier_1_store_mem, inst_classifier_1_reg_reg);

  assign Opcode = instr[6:0];

  // Notes on the sheet:
  //   SType
  //   UType
  //   BType
  //   IType
  //   JType
endmodule
